// Logisim project codificador.circ as structural Verilog: 2 circuits, main circuit main
module main (
  input  bit_E,
  input  bit_1,
  input  bit_2,
  output _0,
  output _1,
  output _2,
  output _3
);

  wire not_1_out, not_2_out;

  not not_1 (not_1_out, bit_1);
  not not_2 (not_2_out, bit_2);
  and and_1 (_0, not_1_out, bit_E, not_2_out);
  and and_2 (_1, bit_1, bit_E, not_2_out);
  and and_3 (_2, not_1_out, bit_E, bit_2);
  and and_4 (_3, bit_1, bit_E, bit_2);

  // Notes on the sheet:
  //   bit_1: pull=up
endmodule

module codificador_2x (
  input  bit_E,
  input  bit_0,
  input  bit_1,
  input  bit_2,
  input  bit_3,
  output _0,
  output _1,
  output _2,
  output _3,
  output _4,
  output _5,
  output _6,
  output _7
);

  wire and_1_out, and_2_out, and_3_out, and_4_out, and_5_out, and_6_out, and_7_out, and_8_out, not_1_out,
       not_2_out, not_3_out, not_4_out;

  not not_1 (not_1_out, bit_1);
  not not_2 (not_2_out, bit_3);
  not not_3 (not_3_out, bit_0);
  not not_4 (not_4_out, bit_2);
  and and_1 (and_1_out, not_3_out, bit_E, not_1_out);
  and and_2 (and_2_out, bit_0, bit_E, not_1_out);
  and and_3 (and_3_out, not_3_out, bit_E, bit_1);
  and and_4 (and_4_out, bit_0, bit_E, bit_1);
  and and_5 (and_5_out, not_4_out, bit_E, not_2_out);
  and and_6 (and_6_out, bit_2, bit_E, not_2_out);
  and and_7 (and_7_out, not_4_out, bit_E, bit_3);
  and and_8 (and_8_out, bit_2, bit_E, bit_3);
  and and_9 (_0, and_1_out, and_5_out);
  and and_10 (_1, and_2_out, and_5_out);
  and and_11 (_2, and_5_out, and_3_out);
  and and_12 (_3, and_4_out, and_5_out);
  and and_13 (_4, and_6_out, and_1_out);
  and and_14 (_5, and_2_out, and_6_out);
  and and_15 (_6, and_3_out, and_6_out);
  and and_16 (_7, and_4_out, and_6_out);

  // Notes on the sheet:
  //   bit_0: pull=up
  //   bit_2: pull=up
  //   este bit sale sobrando
  //   decodificador 2x4
  //   decodificador 2x4
  //   salida 3
  //   salida 0
  //   salida 0
  //   salida 1
  //   salida 2
  //   salida 1
  //   salida 2
  //   salida 3
  //   salida 3x8
endmodule
