// Logisim project multiplexor.circ as structural Verilog: 2 circuits, main circuit main
module main (
  input  entrada_1,
  input  entrada_2,
  input  entrada_3,
  input  entrada_4,
  input  bit_2,
  input  bit_1,
  output salida
);

  wire and_1_out, and_2_out, and_3_out, and_4_out, not_1_out, not_2_out;

  not not_1 (not_1_out, bit_2);
  not not_2 (not_2_out, bit_1);
  and and_1 (and_1_out, entrada_1, not_1_out, not_2_out);
  and and_2 (and_2_out, entrada_2, bit_1, not_1_out);
  and and_3 (and_3_out, entrada_3, not_2_out, bit_2);
  and and_4 (and_4_out, entrada_4, bit_1, bit_2);
  or or_1 (salida, and_1_out, and_2_out, and_3_out, and_4_out);
endmodule

module multiplexor_8x3 (
  input  entrada_0,
  input  entrada_1,
  input  entrada_2,
  input  entrada_3,
  input  entrada_4,
  input  entrada_5,
  input  entrada_6,
  input  entrada_7,
  input  in_9,
  input  in_10,
  input  in_11,
  output salida
);

  wire and_1_out, and_2_out, and_3_out, and_4_out, and_5_out, and_6_out, and_7_out, and_8_out, not_1_out,
       not_2_out, not_3_out, or_1_out, or_2_out;

  not not_1 (not_1_out, in_9);
  not not_2 (not_2_out, in_10);
  not not_3 (not_3_out, in_11);
  and and_1 (and_1_out, not_3_out, not_2_out, not_1_out, entrada_0);
  and and_2 (and_2_out, in_11, not_2_out, not_1_out, entrada_1);
  and and_3 (and_3_out, not_3_out, in_10, not_1_out, entrada_2);
  and and_4 (and_4_out, in_11, in_10, not_1_out, entrada_3);
  and and_5 (and_5_out, in_9, not_2_out, not_3_out, entrada_4);
  and and_6 (and_6_out, in_11, not_2_out, in_9, entrada_5);
  and and_7 (and_7_out, not_3_out, in_10, in_9, entrada_6);
  and and_8 (and_8_out, in_11, in_10, in_9, entrada_7);
  or or_1 (or_1_out, and_1_out, and_2_out, and_3_out, and_4_out);
  or or_2 (or_2_out, and_5_out, and_6_out, and_7_out, and_8_out);
  or or_3 (salida, or_1_out, or_2_out);

  // Notes on the sheet:
  //   bit 3
  //   bit 2
  //   bit 1
endmodule
