// Logisim project sumador.circ as structural Verilog: 2 circuits, main circuit main
module main (
  input  bit_0,
  input  bit_1,
  output resultaddo,
  output acarreo
);

  xor xor_1 (resultaddo, bit_0, bit_1);
  and and_1 (acarreo, bit_0, bit_1);
endmodule

module sumador_de_3_bits (
  input  bit_0,
  input  bit_1,
  input  bit_3,
  output out_4,
  output out_5
);

  wire and_1_out, and_2_out, xor_1_out;

  xor xor_1 (xor_1_out, bit_0, bit_1);
  and and_1 (and_1_out, bit_0, bit_1);
  xor xor_2 (out_4, xor_1_out, bit_3);
  and and_2 (and_2_out, xor_1_out, bit_3);
  or or_1 (out_5, and_1_out, and_2_out);

  // Notes on the sheet:
  //   bit 2
  //   medio sumador
  //   medio sumador
  //   acarreo
  //   acarreo
  //   salida
  //   salida
  //   resultaddo
endmodule
